# Fritzing sketch 6502ctl (saved by Fritzing 0.9.9b)
breadboards: 1

parts:
  W65C02S = DIP - 40 pins [chip_label=W65C02S package="DIP (Dual Inline) [THT]"]
  Part1 = Arduino Mega 2560 (Rev3)

nets:
  N1: W65C02S.VPB, Part1.D30
  N2: W65C02S.RDY, Part1.D22
  N3: W65C02S.PHI1O, Part1.D31
  N4: W65C02S.IRQB, Part1.D23
  N5: W65C02S.MLB, Part1.D32
  N6: W65C02S.NMIB, Part1.D24
  N7: W65C02S.SYNC, Part1.D33
  VDD: W65C02S.VDD, Part1.5V
  N8: W65C02S.A0, Part1.A0
  N9: W65C02S.A1, Part1.A1
  N10: W65C02S.A2, Part1.A2
  N11: W65C02S.A3, Part1.A3
  N12: W65C02S.A4, Part1.A4
  N13: W65C02S.A5, Part1.A5
  N14: W65C02S.A6, Part1.A6
  N15: W65C02S.A7, Part1.A7
  N16: W65C02S.A8, Part1.A8
  N17: W65C02S.A9, Part1.A9
  N18: W65C02S.A10, Part1.A10
  N19: W65C02S.A11, Part1.A11
  VSS: W65C02S.VSS, Part1.GND
  N20: W65C02S.A12, Part1.A12
  N21: W65C02S.A13, Part1.A13
  N22: W65C02S.A14, Part1.A14
  N23: W65C02S.A15, Part1.A15
  N24: W65C02S.D7, Part1.D42
  N25: W65C02S.D6, Part1.D43
  N26: W65C02S.D5, Part1.D44
  N27: W65C02S.D4, Part1.D45
  N28: W65C02S.D3, Part1.D46
  N29: W65C02S.D2, Part1.D47
  N30: W65C02S.D1, Part1.D48
  N31: W65C02S.D0, Part1.D49
  N32: W65C02S.RWB, Part1.D35
  N33: W65C02S.BE, Part1.D28
  N34: W65C02S.PHI2, Part1.D27
  N35: W65C02S.SOB, Part1.D26
  N36: W65C02S.PHI2O, Part1.D34
  N37: W65C02S.RESB, Part1.D25

custom parts:
  DIP - 40 pins: A DIP stand-in part for whatever IC you want. With 40 pins on a 600mil dual inline package (DIP) footprint.
